// Logisim project lab1 testerREV.circ as structural Verilog
module main (
  input  Ci,
  input  in_2,
  output [15:0] out_3,
  output Co
);

  wire adder_2_cout, adder_3_cout, adder_4_cout, adder_5_cout, adder_6_cout, adder_7_cout, adder_8_cout,
       adder_9_cout, adder_10_cout, adder_11_cout, adder_12_cout, adder_14_cout, adder_15_cout,
       adder_16_cout, adder_17_cout, adder_18_cout, adder_19_cout, adder_20_cout, adder_22_cout,
       adder_23_cout, adder_24_cout, adder_25_cout, adder_26_cout, adder_27_cout, adder_28_cout;
  wire [1:0] adder_10_out, adder_11_out, adder_12_out, adder_13_out, adder_27_out, adder_28_out, adder_29_out;
  wire [9:0] adder_22_out;
  wire [15:0] adder_14_out, register_2_q, register_3_q;

  Register #(.width(16)) register_1 ();  // open: D, en, Q, clk, clr
  Register #(.width(16)) register_2 (.Q(register_2_q));  // open: D, en, clk, clr
  Register #(.width(16)) register_3 (.Q(register_3_q));  // open: D, en, clk, clr
  Counter #(.width(16), .max('hffff)) counter_1 ();  // open: load, D, count, Q, carry, clk, clr
  Register #(.width(16)) register_4 (
    .D({adder_13_out, adder_12_out, adder_11_out, adder_10_out, adder_14_out[15:8]}), .clk(in_2));  // open: en, Q, clr
  Register #(.width(16)) register_5 (
    .D({adder_29_out, adder_28_out, adder_27_out, adder_22_out}), .clk(in_2));  // open: en, Q, clr
  Register #(.width(16)) register_6 (.D(adder_14_out), .clk(in_2));  // open: en, Q, clr
  Adder #(.width(16)) adder_1 (.a(register_2_q), .b(register_3_q), .out(out_3), .cin(Ci), .cout(Co));
  Register #(.width(16)) register_7 (.D(out_3), .clk(in_2));  // open: en, Q, clr
  Adder #(.width(1)) adder_2 (
    .a(register_2_q[0]), .b(register_3_q[8]), .out(adder_14_out[8]), .cin(Ci), .cout(adder_2_cout));
  Adder #(.width(1)) adder_3 (
    .a(register_2_q[1]), .b(register_3_q[9]), .out(adder_14_out[9]), .cin(adder_2_cout), .cout(adder_3_cout));
  Adder #(.width(1)) adder_4 (
    .a(register_2_q[2]), .b(register_3_q[10]), .out(adder_14_out[10]), .cin(adder_3_cout), .cout(adder_4_cout));
  Adder #(.width(1)) adder_5 (
    .a(register_2_q[3]), .b(register_3_q[11]), .out(adder_14_out[11]), .cin(adder_4_cout), .cout(adder_5_cout));
  Adder #(.width(1)) adder_6 (
    .a(register_2_q[4]), .b(register_3_q[12]), .out(adder_14_out[12]), .cin(adder_5_cout), .cout(adder_6_cout));
  Adder #(.width(1)) adder_7 (
    .a(register_2_q[5]), .b(register_3_q[13]), .out(adder_14_out[13]), .cin(adder_6_cout), .cout(adder_7_cout));
  Adder #(.width(1)) adder_8 (
    .a(register_2_q[6]), .b(register_3_q[14]), .out(adder_14_out[14]), .cin(adder_7_cout), .cout(adder_8_cout));
  Adder #(.width(1)) adder_9 (
    .a(register_2_q[7]), .b(register_3_q[15]), .out(adder_14_out[15]), .cin(adder_8_cout), .cout(adder_9_cout));
  Adder #(.width(2)) adder_10 (
    .a(register_2_q[9:8]), .b(register_3_q[9:8]), .out(adder_10_out), .cin(adder_9_cout), .cout(adder_10_cout));
  Adder #(.width(2)) adder_11 (
    .a(register_2_q[11:10]), .b(register_3_q[11:10]), .out(adder_11_out), .cin(adder_10_cout),
    .cout(adder_11_cout));
  Adder #(.width(2)) adder_12 (
    .a(register_2_q[13:12]), .b(register_3_q[13:12]), .out(adder_12_out), .cin(adder_11_cout),
    .cout(adder_12_cout));
  Adder #(.width(2)) adder_13 (
    .a(register_2_q[15:14]), .b(register_3_q[15:14]), .out(adder_13_out), .cin(adder_12_cout));  // open: cout
  Adder #(.width(1)) adder_14 (
    .a(register_2_q[8]), .b(register_3_q[0]), .out(adder_14_out[0]), .cin(adder_9_cout), .cout(adder_14_cout));
  Adder #(.width(1)) adder_15 (
    .a(register_2_q[9]), .b(register_3_q[1]), .out(adder_14_out[1]), .cin(adder_14_cout), .cout(adder_15_cout));
  Adder #(.width(1)) adder_16 (
    .a(register_2_q[10]), .b(register_3_q[2]), .out(adder_14_out[2]), .cin(adder_15_cout),
    .cout(adder_16_cout));
  Adder #(.width(1)) adder_17 (
    .a(register_2_q[11]), .b(register_3_q[3]), .out(adder_14_out[3]), .cin(adder_16_cout),
    .cout(adder_17_cout));
  Adder #(.width(1)) adder_18 (
    .a(register_2_q[12]), .b(register_3_q[4]), .out(adder_14_out[4]), .cin(adder_17_cout),
    .cout(adder_18_cout));
  Adder #(.width(1)) adder_19 (
    .a(register_2_q[13]), .b(register_3_q[5]), .out(adder_14_out[5]), .cin(adder_18_cout),
    .cout(adder_19_cout));
  Adder #(.width(1)) adder_20 (
    .a(register_2_q[14]), .b(register_3_q[6]), .out(adder_14_out[6]), .cin(adder_19_cout),
    .cout(adder_20_cout));
  Adder #(.width(1)) adder_21 (
    .a(register_2_q[15]), .b(register_3_q[7]), .out(adder_14_out[7]), .cin(adder_20_cout));  // open: cout
  Adder #(.width(2)) adder_22 (
    .a(register_2_q[1:0]), .b(register_3_q[1:0]), .out(adder_22_out[1:0]), .cin(Ci), .cout(adder_22_cout));
  Adder #(.width(2)) adder_23 (
    .a(register_2_q[3:2]), .b(register_3_q[3:2]), .out(adder_22_out[3:2]), .cin(adder_22_cout),
    .cout(adder_23_cout));
  Adder #(.width(2)) adder_24 (
    .a(register_2_q[5:4]), .b(register_3_q[5:4]), .out(adder_22_out[5:4]), .cin(adder_23_cout),
    .cout(adder_24_cout));
  Adder #(.width(2)) adder_25 (
    .a(register_2_q[7:6]), .b(register_3_q[7:6]), .out(adder_22_out[7:6]), .cin(adder_24_cout),
    .cout(adder_25_cout));
  Adder #(.width(2)) adder_26 (
    .a(register_2_q[9:8]), .b(register_3_q[9:8]), .out(adder_22_out[9:8]), .cin(adder_25_cout),
    .cout(adder_26_cout));
  Adder #(.width(2)) adder_27 (
    .a(register_2_q[11:10]), .b(register_3_q[11:10]), .out(adder_27_out), .cin(adder_26_cout),
    .cout(adder_27_cout));
  Adder #(.width(2)) adder_28 (
    .a(register_2_q[13:12]), .b(register_3_q[13:12]), .out(adder_28_out), .cin(adder_27_cout),
    .cout(adder_28_cout));
  Adder #(.width(2)) adder_29 (
    .a(register_2_q[15:14]), .b(register_3_q[15:14]), .out(adder_29_out), .cin(adder_28_cout));  // open: cout

  // Notes on the sheet:
  //   31
  //   65530
  //   255
  //   65531
  //   A
  //   clock to wake up register
  //   B
  //   true
  //   1/2
  //   2
  //   1
  //   Design: Ben Small 2021
endmodule
